// Logisim project display.circ as structural Verilog: 2 circuits, main circuit main
module main (
  input  in_1
);

  wire and_1_out, and_2_out, clk, demultiplexer_1_out9, fetch, multiplexer_1_out, n_step, no_op;
  wire [2:0] counter_3_q, multiplexer_2_out;
  wire [3:0] counter_2_q, counter_4_q, rgb_video_1_p5;
  wire [4:0] counter_1_q;
  wire [7:0] register_1_q, rom_1_data;

  Counter #(.max('h1f), .width(5)) counter_1 (.Q(counter_1_q), .clk(n_step));  // open: load, D, count, carry, up, clr
  Demultiplexer #(.select(4)) demultiplexer_1 (
    .out0(no_op), .out1(fetch), .out8(n_step), .out9(demultiplexer_1_out9), .in(1'b1), .sel(counter_2_q));  // open: out2, out3, out4, out5, out6, out7, out10, out11, out12, out13, out14, out15
  Counter #(.max('hf), .width(4)) counter_2 (
    .Q(counter_2_q), .clk(clk), .clr(demultiplexer_1_out9));  // open: load, D, count, carry, up
  Clock clock_1 (.out(clk));
  ROM #(.addrWidth(5)) rom_1 (.addr(counter_1_q), .data(rom_1_data));
  and and_1 (and_1_out, clk, ~no_op, ~fetch);  // AND_Gate
  Register register_1 (.D(rom_1_data), .clk(fetch), .Q(register_1_q));  // open: en, clr
  Counter #(.max('h7), .width(3)) counter_3 (.Q(counter_3_q), .clk(and_1_out));  // open: load, D, count, carry, up, clr
  Multiplexer #(.select(3)) multiplexer_1 (
    .in0(register_1_q[7]), .in1(register_1_q[6]), .in2(register_1_q[5]), .in3(register_1_q[4]),
    .in4(register_1_q[3]), .in5(register_1_q[2]), .in6(register_1_q[1]), .in7(register_1_q[0]),
    .out(multiplexer_1_out), .sel(counter_3_q));
  Counter #(.max('hf), .width(4)) counter_4 (.Q(counter_4_q), .clk(and_1_out));  // open: load, D, count, carry, up, clr
  and and_2 (and_2_out, counter_4_q[3], counter_4_q[2], counter_4_q[1], counter_4_q[0]);
  Multiplexer #(.width(3)) multiplexer_2 (.in0(3'b000), .in1(3'b111), .out(multiplexer_2_out), .sel(multiplexer_1_out));
  // RGB_Video #(.cursor("No Cursor"), .height(16), .scale(8), .width(16)) rgb_video_1: pin names not known; wires that end beside it: in_1, clk, 1'b1, counter_4_q, rgb_video_1_p5, multiplexer_2_out
  Counter #(.max('hf), .trigger("falling"), .width(4)) counter_5 (
    .Q(rgb_video_1_p5), .clk(and_2_out));  // open: load, D, count, carry, up, clr

  // Notes on the sheet:
  //   contents of rom_1 (hex, n*v repeats v):
  //   ff 30*0 ff
endmodule

module display2 (
  input  in_1,
  input  in_2,
  input  [2:0] in_3,
  input  [7:0] in_4,
  input  [7:0] in_5
);

  wire and_1_out, and_2_out, clk, demultiplexer_1_out17, fetch, multiplexer_1_out, next_step, no_op;
  wire [2:0] multiplexer_2_out;
  wire [3:0] counter_3_q;
  wire [4:0] counter_1_q;
  wire [7:0] counter_4_q, counter_5_q;
  wire [11:0] counter_2_q;
  wire [15:0] ram_1_dout, register_1_q;

  Clock clock_1 (.out(clk));
  Demultiplexer #(.select(5)) demultiplexer_1 (
    .out0(no_op), .out1(fetch), .out16(next_step), .out17(demultiplexer_1_out17), .in(1'b1), .sel(counter_1_q));  // open: out2, out3, out4, out5, out6, out7, out8, out9, out10, out11, out12, out13, out14, out15, out18, out19, out20, out21, out22, out23, out24, out25, out26, out27, out28, out29, out30, out31
  Counter #(.max('h1f), .width(5)) counter_1 (
    .Q(counter_1_q), .clk(clk), .clr(demultiplexer_1_out17));  // open: load, D, count, carry, up
  Counter #(.max('hfff), .width(12)) counter_2 (
    .Q(counter_2_q), .clk(next_step));  // open: load, D, count, carry, up, clr
  RAM #(.addrWidth(12), .dataWidth(16), .trigger("high")) ram_1 (
    .addr(counter_2_q), .dout(ram_1_dout));  // open: we, oe, din
  and and_1 (and_1_out, ~no_op, ~fetch, clk);  // AND_Gate
  Register #(.width(16)) register_1 (.D(ram_1_dout), .clk(fetch), .Q(register_1_q));  // open: en, clr
  Counter #(.max('hf), .width(4)) counter_3 (.Q(counter_3_q), .clk(and_1_out));  // open: load, D, count, carry, up, clr
  Counter counter_4 (.Q(counter_4_q), .clk(and_1_out));  // open: load, D, count, carry, up, clr
  Multiplexer #(.select(4)) multiplexer_1 (
    .in0(register_1_q[15]), .in1(register_1_q[14]), .in2(register_1_q[13]), .in3(register_1_q[12]),
    .in4(register_1_q[11]), .in5(register_1_q[10]), .in6(register_1_q[9]), .in7(register_1_q[8]),
    .in8(register_1_q[7]), .in9(register_1_q[6]), .in10(register_1_q[5]), .in11(register_1_q[4]),
    .in12(register_1_q[3]), .in13(register_1_q[2]), .in14(register_1_q[1]), .in15(register_1_q[0]),
    .out(multiplexer_1_out), .sel(counter_3_q));
  and and_2 (and_2_out, counter_4_q[7], counter_4_q[6], counter_4_q[5], counter_4_q[4], counter_4_q[3], counter_4_q[2], counter_4_q[1], counter_4_q[0]);
  Counter #(.trigger("falling")) counter_5 (.Q(counter_5_q), .clk(and_2_out));  // open: load, D, count, carry, up, clr
  Multiplexer #(.width(3)) multiplexer_2 (.in0(3'b000), .in1(3'b111), .out(multiplexer_2_out), .sel(multiplexer_1_out));
  // RGB_Video #(.cursor("No Cursor"), .height(256), .scale(3), .width(256)) rgb_video_1: pin names not known; wires that end beside it: in_1, clk, 1'b1, counter_4_q, counter_5_q, multiplexer_2_out
  // RGB_Video #(.cursor("No Cursor"), .height(256), .scale(3), .width(256)) rgb_video_2: pin names not known; wires that end beside it: 1'b0, in_2, 1'b1, in_4, in_5, in_3
endmodule
