// Logisim project misc16bit.circ as structural Verilog: 3 circuits, main circuit main
module main (
  input  [11:0] in_1,
  output [15:0] out_2
);

  wire and_1_out, and_2_out, and_3_out, and_4_out, and_5_out, and_6_out, and_8_out, and_9_out, and_10_out,
       and_11_out, and_12_out, and_13_out, and_14_out, and_15_out, and_16_out, and_17_out, and_18_out,
       and_19_out, and_20_out, and_21_out, and_22_out, and_23_out, and_24_out, and_25_out, and_26_out,
       and_27_out, and_28_out, and_29_out, and_30_out, and_32_out, and_33_out, and_34_out, and_35_out,
       and_36_out, and_38_out, and_39_out, and_40_out, clk, clk_display, control_unit_1_add_instr,
       control_unit_1_and_instr, control_unit_1_or_instr, control_unit_1_sub_instr, d_store_instr, data_flag,
       data_instr_out, demultiplexer_1_out4, demultiplexer_1_out5, demultiplexer_3_out17, e_D, e_KR, e_R0,
       e_R1, e_R2, execute, fetch, fetch_bits, inc_IAR, jump_instr, jz_instr, KR_clk, load_instr, move_instr,
       multiplexer_4_out, multiplexer_6_out, next_step, ng_flag, no_op, one_reg, or_1_out, or_2_out,
       or_3_out, or_4_out, or_5_out, or_6_out, or_7_out, or_8_out, or_9_out, or_10_out, or_11_out, or_12_out,
       or_13_out, or_14_out, or_15_out, or_16_out, s_DAR, s_JAR, s_MAR, s_R0, s_R1, s_R2, store_instr,
       two_reg, W_out, write, z_flag;
  wire [2:0] counter_1_q, multiplexer_7_out;
  wire [3:0] counter_4_q, dest_reg;
  wire [4:0] counter_3_q;
  wire [7:0] counter_5_q, counter_6_q;
  wire [11:0] counter_2_q, multiplexer_5_out;
  wire [14:0] pull_resistor_1_node;
  wire [15:0] adder_1_out, D_reg_value, DAR_q, demultiplexer_2_out0, demultiplexer_2_out1, IAR_q, instr,
       JAR_q, KR_in, KR_q, MAR_q, multiplexer_1_out, multiplexer_2_out, multiplexer_3_out, R0_reg_value,
       R1_reg_value, R2_reg_value, ram_1_dout, ram_2_dout, register_1_q, register_2_q, rom_1_data;

  Pull_Resistor pull_resistor_1 (.node({ng_flag, pull_resistor_1_node}));
  Register #(.width(16)) MAR (.D({ng_flag, pull_resistor_1_node}), .en(and_1_out), .Q(MAR_q));  // open: clk, clr
  and and_1 (and_1_out, s_MAR, execute, move_instr);
  // Probe on {ng_flag, pull_resistor_1_node}
  Counter #(.max('h7), .width(3)) counter_1 (
    .Q(counter_1_q), .clk(clk), .clr(demultiplexer_1_out5));  // open: load, D, count, carry, up
  Button button_1 ();  // open: out
  Clock clock_1 (.out(clk));
  ROM #(.addrWidth(16), .dataWidth(16)) rom_1 (.addr(IAR_q), .data(rom_1_data));
  and and_2 (and_2_out, store_instr, execute);
  RAM #(.addrWidth(16), .dataWidth(16), .trigger("high")) ram_1 (
    .addr(MAR_q), .we(and_2_out), .din({ng_flag, pull_resistor_1_node}), .dout(ram_1_dout));  // open: oe
  and and_3 (and_3_out, jz_instr, z_flag);
  and and_4 (and_4_out, jump_instr, execute);
  Demultiplexer #(.select(3)) demultiplexer_1 (
    .out1(fetch), .out2(execute), .out3(write), .out4(demultiplexer_1_out4), .out5(demultiplexer_1_out5),
    .in(1'b1), .sel(counter_1_q));  // open: out0, out6, out7
  and and_5 (and_5_out, jz_instr, z_flag);
  Adder #(.width(16)) adder_1 (.a(16'h1), .b(IAR_q), .out(adder_1_out));  // open: cin, cout
  Multiplexer #(.width(16)) multiplexer_1 (.in0(adder_1_out), .in1(JAR_q), .out(multiplexer_1_out), .sel(or_1_out));
  or or_1 (or_1_out, jump_instr, and_3_out);
  or or_2 (or_2_out, inc_IAR, and_4_out, and_6_out);
  and and_6 (and_6_out, jz_instr, z_flag, execute);
  or or_3 (or_3_out, jump_instr, and_5_out);
  Register #(.width(16)) IAR (.D(multiplexer_1_out), .clk(or_2_out), .Q(IAR_q));  // open: en, clr
  and and_7 (inc_IAR, demultiplexer_1_out4, ~or_3_out);  // AND_Gate
  Demultiplexer #(.width(16)) demultiplexer_2 (
    .out0(demultiplexer_2_out0), .out1(demultiplexer_2_out1), .in(rom_1_data), .sel(data_flag));
  and and_8 (and_8_out, fetch, data_flag);
  Register #(.width(16)) D (.D(demultiplexer_2_out1), .clk(and_8_out), .Q(D_reg_value));  // open: en, clr
  and and_9 (and_9_out, e_D, move_instr);
  and and_10 (and_10_out, e_D, store_instr);
  assign {ng_flag, pull_resistor_1_node} = load_instr ? ram_1_dout : 16'bz;  // Controlled_Buffer controlled_buffer_1
  assign {ng_flag, pull_resistor_1_node} = or_4_out ? D_reg_value : 16'bz;  // Controlled_Buffer controlled_buffer_2
  or or_4 (or_4_out, and_9_out, and_10_out);
  or or_5 (or_5_out, and_13_out, and_11_out, and_12_out);
  and and_11 (and_11_out, s_R0, execute, load_instr);
  Register #(.width(16)) R0 (.D({ng_flag, pull_resistor_1_node}), .clk(or_5_out), .Q(R0_reg_value));  // open: en, clr
  and and_12 (and_12_out, s_R0, execute, move_instr);
  and and_13 (and_13_out, s_R0, write, or_7_out);
  and and_14 (and_14_out, e_R0, move_instr);
  and and_15 (and_15_out, e_R0, jz_instr);
  and and_16 (and_16_out, e_R0, store_instr);
  Multiplexer #(.select(4), .width(16)) multiplexer_2 (
    .in2(R0_reg_value), .in3(R1_reg_value), .in4(R2_reg_value), .out(multiplexer_2_out), .sel(dest_reg));  // open: in0, in1, in5, in6, in7, in8, in9, in10, in11, in12, in13, in14, in15
  Multiplexer #(.select(4), .width(16)) multiplexer_3 (
    .in2(R0_reg_value), .in3(R1_reg_value), .in4(R2_reg_value), .out(multiplexer_3_out), .sel(instr[7:4]));  // open: in0, in1, in5, in6, in7, in8, in9, in10, in11, in12, in13, in14, in15
  Register #(.width(16)) IR (
    .D(demultiplexer_2_out0), .clk(fetch), .Q({instr[15:12], dest_reg, instr[7:0]}));  // open: en, clr
  or or_6 (or_6_out, and_14_out, and_16_out, and_15_out, and_17_out);
  assign {ng_flag, pull_resistor_1_node} = or_6_out ? R0_reg_value : 16'bz;  // Controlled_Buffer controlled_buffer_3
  and and_17 (and_17_out, d_store_instr, e_R0);
  or or_7 (or_7_out, two_reg, one_reg);
  or or_8 (or_8_out, and_20_out, and_21_out, and_19_out);
  Register #(.width(16)) R1 (.D({ng_flag, pull_resistor_1_node}), .clk(or_8_out), .Q(R1_reg_value));  // open: en, clr
  and and_18 (and_18_out, e_R1, move_instr);
  and and_19 (and_19_out, s_R1, execute, move_instr);
  and and_20 (and_20_out, s_R1, write, or_9_out);
  or or_9 (or_9_out, two_reg, one_reg);
  and and_21 (and_21_out, s_R1, execute, load_instr);
  or or_10 (or_10_out, and_18_out, and_22_out, and_23_out, and_24_out);
  and and_22 (and_22_out, e_R1, store_instr);
  and and_23 (and_23_out, e_R1, jz_instr);
  and and_24 (and_24_out, d_store_instr, e_R1);
  and data_instr (data_instr_out, instr[12], ~instr[13], ~instr[14], ~instr[15]);  // AND_Gate
  Register #(.width(16)) R2 (.D({ng_flag, pull_resistor_1_node}), .clk(or_11_out), .Q(R2_reg_value));  // open: en, clr
  assign {ng_flag, pull_resistor_1_node} = or_10_out ? R1_reg_value : 16'bz;  // Controlled_Buffer controlled_buffer_4
  and and_25 (and_25_out, s_R2, execute, move_instr);
  or or_11 (or_11_out, and_26_out, and_27_out, and_25_out);
  Multiplexer multiplexer_4 (.in0(data_instr_out), .in1(1'b0), .out(multiplexer_4_out), .sel(data_flag));
  and and_26 (and_26_out, s_R2, write, or_13_out);
  and and_27 (and_27_out, s_R2, execute, load_instr);
  alu alu_1 (.x(multiplexer_2_out), .y(multiplexer_3_out), .opcode(instr[15:12]), .o(out_2));
  D_Flip_Flop d_ff_1 (.D(multiplexer_4_out), .clk(execute), .Q(data_flag));  // open: Qn, preset, reset
  and and_28 (and_28_out, e_R2, move_instr);
  and and_29 (and_29_out, e_R2, store_instr);
  and and_30 (and_30_out, e_R2, jz_instr);
  or or_12 (or_12_out, and_28_out, and_29_out, and_30_out);
  assign {ng_flag, pull_resistor_1_node} = or_12_out ? R2_reg_value : 16'bz;  // Controlled_Buffer controlled_buffer_5
  // AND_Gate and_31 has open pins: in0=e_R2, in1=d_store_instr, out=open
  Register #(.width(16)) register_1 (.D(out_2), .clk(and_32_out), .Q(register_1_q));  // open: en, clr
  and and_32 (and_32_out, execute, or_14_out);
  Register #(.width(16)) JAR (.D({ng_flag, pull_resistor_1_node}), .clk(and_33_out), .Q(JAR_q));  // open: en, clr
  and and_33 (and_33_out, s_JAR, execute, move_instr);
  or or_13 (or_13_out, two_reg, one_reg);
  or or_14 (or_14_out, two_reg, one_reg);
  Register #(.trigger("high"), .width(16)) KR (.D(KR_in), .clk(1'b1), .Q(KR_q));  // open: en, clr
  and and_34 (and_34_out, e_KR, move_instr);
  assign {ng_flag, pull_resistor_1_node} = and_34_out ? KR_q : 16'bz;  // Controlled_Buffer controlled_buffer_6
  or or_15 (or_15_out, ng_flag, pull_resistor_1_node[14], pull_resistor_1_node[13], pull_resistor_1_node[12], pull_resistor_1_node[11], pull_resistor_1_node[10], pull_resistor_1_node[9], pull_resistor_1_node[8], pull_resistor_1_node[7], pull_resistor_1_node[6], pull_resistor_1_node[5], pull_resistor_1_node[4], pull_resistor_1_node[3], pull_resistor_1_node[2], pull_resistor_1_node[1], pull_resistor_1_node[0]);
  not not_1 (z_flag, or_15_out);
  Register #(.width(16)) DAR (.D({ng_flag, pull_resistor_1_node}), .clk(and_35_out), .Q(DAR_q));  // open: en, clr
  and and_35 (and_35_out, s_DAR, execute, move_instr);
  assign KR_in = KR_clk ? 16'h51 : 16'bz;  // Controlled_Buffer controlled_buffer_7
  Button Q (.out(KR_clk));
  Pull_Resistor pull_resistor_2 (.node(KR_in));
  assign KR_in = W_out ? 16'h57 : 16'bz;  // Controlled_Buffer controlled_buffer_8
  Button W (.out(W_out));
  assign {ng_flag, pull_resistor_1_node} = and_36_out ? register_1_q : 16'bz;  // Controlled_Buffer controlled_buffer_9
  control_unit control_unit_1 (
    .instr({instr[15:12], dest_reg, instr[7:0]}), .e_D(e_D), .e_R0(e_R0), .e_R1(e_R1), .e_R2(e_R2),
    .e_KR(e_KR), .s_R0(s_R0), .s_R1(s_R1), .s_R2(s_R2), .s_MAR(s_MAR), .s_JAR(s_JAR), .s_DAR(s_DAR),
    .move_instr(move_instr), .add_instr(control_unit_1_add_instr), .sub_instr(control_unit_1_sub_instr),
    .and_instr(control_unit_1_and_instr), .or_instr(control_unit_1_or_instr), .not_instr(one_reg),
    .load_instr(load_instr), .store_instr(store_instr), .jump_instr(jump_instr), .jz_instr(jz_instr),
    .d_store_instr(d_store_instr));
  and and_36 (and_36_out, write, or_16_out);
  or two_regs (two_reg, control_unit_1_add_instr, control_unit_1_sub_instr, control_unit_1_and_instr, control_unit_1_or_instr);
  or or_16 (or_16_out, two_reg, one_reg);
  Clock clock_2 ();  // open: out
  and and_37 (clk_display, clk, ~d_store_instr);  // AND_Gate
  Counter #(.max('hfff), .width(12)) counter_2 (
    .Q(counter_2_q), .clk(next_step));  // open: load, D, count, carry, up, clr
  Demultiplexer #(.select(5)) demultiplexer_3 (
    .out0(no_op), .out1(fetch_bits), .out16(next_step), .out17(demultiplexer_3_out17), .in(1'b1),
    .sel(counter_3_q));  // open: out2, out3, out4, out5, out6, out7, out8, out9, out10, out11, out12, out13, out14, out15, out18, out19, out20, out21, out22, out23, out24, out25, out26, out27, out28, out29, out30, out31
  Counter #(.max('h1f), .width(5)) counter_3 (
    .Q(counter_3_q), .clk(clk_display), .clr(demultiplexer_3_out17));  // open: load, D, count, carry, up
  Multiplexer #(.width(12)) multiplexer_5 (
    .in0(counter_2_q), .in1(DAR_q[11:0]), .out(multiplexer_5_out), .sel(d_store_instr));
  // Probe on in_1
  RAM #(.addrWidth(12), .dataWidth(16), .trigger("high")) ram_2 (
    .addr(multiplexer_5_out), .we(and_38_out), .din({ng_flag, pull_resistor_1_node}), .dout(ram_2_dout));  // open: oe
  and and_38 (and_38_out, d_store_instr, execute);
  Register #(.width(16)) register_2 (.D(ram_2_dout), .clk(fetch_bits), .Q(register_2_q));  // open: en, clr
  Counter #(.max('hf), .width(4)) counter_4 (
    .Q(counter_4_q), .clk(and_39_out));  // open: load, D, count, carry, up, clr
  and and_39 (and_39_out, ~no_op, ~fetch_bits, clk_display);  // AND_Gate
  Multiplexer #(.select(4)) multiplexer_6 (
    .in0(register_2_q[15]), .in1(register_2_q[14]), .in2(register_2_q[13]), .in3(register_2_q[12]),
    .in4(register_2_q[11]), .in5(register_2_q[10]), .in6(register_2_q[9]), .in7(register_2_q[8]),
    .in8(register_2_q[7]), .in9(register_2_q[6]), .in10(register_2_q[5]), .in11(register_2_q[4]),
    .in12(register_2_q[3]), .in13(register_2_q[2]), .in14(register_2_q[1]), .in15(register_2_q[0]),
    .out(multiplexer_6_out), .sel(counter_4_q));
  Counter counter_5 (.Q(counter_5_q), .clk(and_39_out));  // open: load, D, count, carry, up, clr
  and and_40 (and_40_out, counter_5_q[7], counter_5_q[6], counter_5_q[5], counter_5_q[4], counter_5_q[3], counter_5_q[2], counter_5_q[1], counter_5_q[0]);
  Counter #(.trigger("falling")) counter_6 (.Q(counter_6_q), .clk(and_40_out));  // open: load, D, count, carry, up, clr
  Multiplexer #(.width(3)) multiplexer_7 (.in0(3'b000), .in1(3'b111), .out(multiplexer_7_out), .sel(multiplexer_6_out));
  // RGB_Video #(.cursor("No Cursor"), .height(256), .width(256)) rgb_video_1: pin names not known; wires that end beside it: 1'b0, clk_display, 1'b1, counter_5_q, counter_6_q, multiplexer_7_out

  // Other names for the same wires on the sheet: instr[11:8] = dest_reg; src_reg[3:0] = instr[7:4]

  // Notes on the sheet:
  //   contents of rom_1 (hex, n*v repeats v):
  //   c020
  //   Эта общая шина нужна для того чтобы реализовать команду move
endmodule

module control_unit (
  input  [15:0] instr,
  output e_D,
  output e_R0,
  output e_R1,
  output e_R2,
  output e_KR,
  output s_R0,
  output s_R1,
  output s_R2,
  output s_MAR,
  output s_JAR,
  output s_DAR,
  output move_instr,
  output add_instr,
  output sub_instr,
  output and_instr,
  output or_instr,
  output not_instr,
  output load_instr,
  output store_instr,
  output jump_instr,
  output jz_instr,
  output d_store_instr
);

  and move (move_instr, ~instr[15], ~instr[14], instr[13], ~instr[12]);  // AND_Gate
  and not_i (not_instr, ~instr[15], instr[14], instr[13], instr[12]);  // AND_Gate
  and add (add_instr, ~instr[15], ~instr[14], instr[13], instr[12]);  // AND_Gate
  and load (load_instr, instr[15], ~instr[14], ~instr[13], ~instr[12]);  // AND_Gate
  and sub (sub_instr, ~instr[15], instr[14], ~instr[13], ~instr[12]);  // AND_Gate
  and store (store_instr, instr[15], ~instr[14], ~instr[13], instr[12]);  // AND_Gate
  Demultiplexer #(.select(4)) demultiplexer_1 (
    .out2(s_R0), .out3(s_R1), .out4(s_R2), .out5(s_MAR), .out7(s_JAR), .out9(s_DAR), .in(1'b1),
    .sel(instr[11:8]));  // open: out0, out1, out6, out8, out10, out11, out12, out13, out14, out15
  Demultiplexer #(.select(4)) demultiplexer_2 (
    .out1(e_D), .out2(e_R0), .out3(e_R1), .out4(e_R2), .out8(e_KR), .in(1'b1), .sel(instr[7:4]));  // open: out0, out5, out6, out7, out9, out10, out11, out12, out13, out14, out15
  and and_i (and_instr, ~instr[15], instr[14], ~instr[13], instr[12]);  // AND_Gate
  and jump (jump_instr, instr[15], ~instr[14], instr[13], ~instr[12]);  // AND_Gate
  and or_i (or_instr, ~instr[15], instr[14], instr[13], ~instr[12]);  // AND_Gate
  and jz (jz_instr, instr[15], ~instr[14], instr[13], instr[12]);  // AND_Gate
  and d_store (d_store_instr, instr[15], instr[14], ~instr[13], ~instr[12]);  // AND_Gate

  // Other names for the same wires on the sheet: dest_reg[3:0] = instr[11:8]; source_reg[3:0] = instr[7:4]

  // Notes on the sheet:
  //   move instruction
endmodule

module alu (
  input  [15:0] x,
  input  [15:0] y,
  input  [3:0] opcode,
  output [15:0] o
);

  wire [15:0] adder_1_out, and_1_out, not_1_out, or_1_out, subtractor_1_out;

  Adder #(.width(16)) adder_1 (.a(x), .b(y), .out(adder_1_out));  // open: cin, cout
  Subtractor #(.width(16)) subtractor_1 (.a(x), .b(y), .out(subtractor_1_out));  // open: bin, bout
  assign and_1_out = x & y;  // AND_Gate and_1, 16 bits wide
  assign or_1_out = x | y;  // OR_Gate or_1, 16 bits wide
  assign not_1_out = ~x;  // NOT_Gate not_1, 16 bits wide
  Multiplexer #(.select(4), .width(16)) multiplexer_1 (
    .in3(adder_1_out), .in4(subtractor_1_out), .in5(and_1_out), .in6(or_1_out), .in7(not_1_out), .out(o),
    .sel(opcode));  // open: in0, in1, in2, in8, in9, in10, in11, in12, in13, in14, in15
endmodule
